// Logisim project mine_de_rien.circ as structural Verilog: 5 circuits, main circuit main
module main (
  input  [63:0] trainPresence0,
  input  [5:0] sectionAddress,
  input  C0,
  output S3
);

  wire section0To7Deactivated, section8To15Deactivated, section16To23Deactivated;

  c_138 c_138_1 (
    .G2B(1'b0), .G2A(C0), .G1(1'b1), .A(sectionAddress[3]), .B(sectionAddress[4]), .C(sectionAddress[5]),
    .Y0(section0To7Deactivated), .Y1(section8To15Deactivated), .Y2(section16To23Deactivated));  // open: Y3, Y4, Y5, Y6, Y7
  trainPresenceDetector8Bits section0To7 (
    .trainPresence(trainPresence0[7:0]), .A(sectionAddress[0]), .B(sectionAddress[1]), .C(sectionAddress[2]),
    .strobe(section0To7Deactivated), .S3(S3));
  trainPresenceDetector8Bits section8To15 (
    .trainPresence(trainPresence0[15:8]), .A(sectionAddress[0]), .B(sectionAddress[1]),
    .C(sectionAddress[2]), .strobe(section8To15Deactivated), .S3(S3));
  trainPresenceDetector8Bits section16To23 (
    .trainPresence(trainPresence0[23:16]), .A(sectionAddress[0]), .B(sectionAddress[1]),
    .C(sectionAddress[2]), .strobe(section16To23Deactivated), .S3(S3));

  // Other names for the same wires on the sheet: latch = C0; D0 = sectionAddress[0]; D1 = sectionAddress[1];
  //   D2 = sectionAddress[2]; D3 = sectionAddress[3]; D4 = sectionAddress[4]; D5 = sectionAddress[5];
  //   trainNotPresent = S3; trainPresence[63:0] = trainPresence0; trainPresence0To7[7:0] = trainPresence0[7:0];
  //   trainPresence8To15[7:0] = trainPresence0[15:8]; trainPresence16To23[7:0] = trainPresence0[23:16];
  //   trainPresence24To31[7:0] = trainPresence0[31:24]; trainPresence32To39[7:0] = trainPresence0[39:32]
endmodule

module c_2804 (
  input  IN1,
  input  IN2,
  input  IN3,
  input  IN4,
  input  IN5,
  input  IN6,
  input  IN7,
  input  IN8,
  output OUT1,
  output OUT2,
  output OUT3,
  output OUT4,
  output OUT5,
  output OUT6,
  output OUT7,
  output OUT8
);

  not not_1 (OUT1, IN1);
  not not_2 (OUT2, IN2);
  not not_3 (OUT3, IN3);
  not not_4 (OUT4, IN4);
  not not_5 (OUT5, IN5);
  not not_6 (OUT6, IN6);
  not not_7 (OUT7, IN7);
  not not_8 (OUT8, IN8);
endmodule

module trainPresenceDetector8Bits (
  input  [7:0] trainPresence,
  input  A,
  input  B,
  input  C,
  input  strobe,
  output S3
);

  wire c_2804_1_out1, c_2804_1_out2, c_2804_1_out3, c_2804_1_out4, c_2804_1_out5, c_2804_1_out6,
       c_2804_1_out7, c_2804_1_out8, not_1_out, section0To7_y;

  not not_1 (not_1_out, strobe);
  c_2804 c_2804_1 (
    .IN1(trainPresence[0]), .IN2(trainPresence[1]), .IN3(trainPresence[2]), .IN4(trainPresence[3]),
    .IN5(trainPresence[4]), .IN6(trainPresence[5]), .IN7(trainPresence[6]), .IN8(trainPresence[7]),
    .OUT1(c_2804_1_out1), .OUT2(c_2804_1_out2), .OUT3(c_2804_1_out3), .OUT4(c_2804_1_out4),
    .OUT5(c_2804_1_out5), .OUT6(c_2804_1_out6), .OUT7(c_2804_1_out7), .OUT8(c_2804_1_out8));
  c_251 section0To7 (
    .D0(c_2804_1_out1), .D1(c_2804_1_out2), .D2(c_2804_1_out3), .D3(c_2804_1_out4), .D4(c_2804_1_out5),
    .D5(c_2804_1_out6), .D6(c_2804_1_out7), .D7(c_2804_1_out8), .A(A), .B(B), .C(C), .STROBE(not_1_out),
    .Y(section0To7_y));  // open: W
  Multiplexer multiplexer_1 (.in1(section0To7_y), .out(S3), .sel(not_1_out));  // open: in0
endmodule

module c_251 (
  input  D0,
  input  D1,
  input  D2,
  input  D3,
  input  D4,
  input  D5,
  input  D6,
  input  D7,
  input  A,
  input  B,
  input  C,
  input  STROBE,
  output Y,
  output W
);

  Multiplexer #(.enable("true"), .select(3)) multiplexer_1 (
    .in0(D0), .in1(D1), .in2(D2), .in3(D3), .in4(D4), .in5(D5), .in6(D6), .in7(D7), .out(Y), .sel({C, B, A}),
    .en(STROBE));
  not not_1 (W, Y);
endmodule

module c_138 (
  input  G2B,
  input  G2A,
  input  G1,
  input  A,
  input  B,
  input  C,
  output Y0,
  output Y1,
  output Y2,
  output Y3,
  output Y4,
  output Y5,
  output Y6,
  output Y7
);

  wire and_1_out, demultiplexer_1_out0, demultiplexer_1_out1, demultiplexer_1_out2, demultiplexer_1_out3,
       demultiplexer_1_out4, demultiplexer_1_out5, demultiplexer_1_out6, demultiplexer_1_out7;

  and and_1 (and_1_out, ~G2B, ~G2A, G1);  // AND_Gate
  Demultiplexer #(.select(3)) demultiplexer_1 (
    .out0(demultiplexer_1_out0), .out1(demultiplexer_1_out1), .out2(demultiplexer_1_out2),
    .out3(demultiplexer_1_out3), .out4(demultiplexer_1_out4), .out5(demultiplexer_1_out5),
    .out6(demultiplexer_1_out6), .out7(demultiplexer_1_out7), .in(and_1_out), .sel({C, B, A}));
  not not_1 (Y0, demultiplexer_1_out0);
  not not_2 (Y1, demultiplexer_1_out1);
  not not_3 (Y2, demultiplexer_1_out2);
  not not_4 (Y3, demultiplexer_1_out3);
  not not_5 (Y4, demultiplexer_1_out4);
  not not_6 (Y5, demultiplexer_1_out5);
  not not_7 (Y6, demultiplexer_1_out6);
  not not_8 (Y7, demultiplexer_1_out7);
endmodule
